// Logisim project Final_Project.circ as structural Verilog: 14 circuits, main circuit main
module main (
  output Output_1
);

  wire and_1_out, and_2_out, and_3_out, and_5_out, and_6_out, Button_1_out, clk, clock_2_out, clock_3_out,
       end_cycle_a, end_cycle_b, G, Gb, not_1_out, or_1_out, or_2_out, or_3_out, or_4_out,
       pedestrian_button_1_en, pedestrian_clock, R, Rb, RGBLED_5_p5, Y, Yb;
  wire [3:0] DownCounter_v1_1_count, Mod5_Counter_1_output_bus_1, multiplexer_1_out, multiplexer_2_out;
  wire [7:0] HEX0, HEX1;

  Clock clock_1 (.out(clk));
  Button Button_1 (.out(Button_1_out));
  D_Flip_Flop d_ff_1 (.clk(clock_2_out), .Q(Output_1), .preset(Button_1_out), .reset(pedestrian_clock));  // open: D, Qn
  Clock clock_2 (.out(clock_2_out));
  not not_1 (not_1_out, pedestrian_clock);
  or or_1 (or_1_out, end_cycle_b, end_cycle_a);
  and and_1 (and_1_out, ~multiplexer_1_out[0], ~multiplexer_1_out[1], ~multiplexer_1_out[2], ~multiplexer_1_out[3]);  // AND_Gate
  Multiplexer #(.width(4)) multiplexer_1 (
    .in0(DownCounter_v1_1_count), .in1(4'b0011), .out(multiplexer_1_out), .sel(pedestrian_clock));
  and and_2 (and_2_out, Output_1, ~pedestrian_button_1_en, or_1_out);  // AND_Gate
  or or_2 (or_2_out, pedestrian_clock, R);
  // RGBLED RGBLED_1: pin names not known; wires that end beside it: or_2_out
  and and_3 (and_3_out, Y, ~pedestrian_clock);  // AND_Gate
  // RGBLED RGBLED_3: pin names not known; wires that end beside it: and_3_out, and_3_out
  // RGBLED RGBLED_5: pin names not known; wires that end beside it: multiplexer_1_out[0], multiplexer_1_out[1], multiplexer_1_out[2], multiplexer_1_out[3], RGBLED_5_p5
  and and_4 (RGBLED_5_p5, G, ~pedestrian_clock);  // AND_Gate
  Clock clock_3 (.out(clock_3_out));
  or or_3 (or_3_out, and_2_out, pedestrian_clock);
  and and_5 (and_5_out, Yb, ~pedestrian_clock);  // AND_Gate
  and and_6 (and_6_out, Gb, ~pedestrian_clock);  // AND_Gate
  FSM2 FSM2_1 (
    .en(and_1_out), .next_state(clock_3_out), .Ra(R), .Ya(Y), .end_cycle_a(end_cycle_a), .Ga(G), .Rb(Rb),
    .Yb(Yb), .end_cycle_b(end_cycle_b), .Gb(Gb));
  or or_4 (or_4_out, pedestrian_clock, Rb);
  // RGBLED RGBLED_2: pin names not known; wires that end beside it: or_4_out
  // RGBLED RGBLED_4: pin names not known; wires that end beside it: and_5_out, and_5_out
  // RGBLED RGBLED_6: pin names not known; wires that end beside it: and_6_out
  Mod5_Counter Mod5_Counter_1 (
    .E(or_3_out), .Clk(clk), .five_2ndcomp(4'b1011), .Output_bus_1(Mod5_Counter_1_output_bus_1));
  DownCounter_v1 DownCounter_v1_1 (.en(not_1_out), .clk(clk), .count(DownCounter_v1_1_count));
  pedestrian_button pedestrian_button_1 (.counter(DownCounter_v1_1_count), .en(pedestrian_button_1_en));
  _7_Segment_Display #(.active("false")) L_7_Segment_Display_1 (
    .g(HEX1[6]), .f(HEX1[5]), .a(HEX1[0]), .b(HEX1[1]), .e(HEX1[4]), .d(HEX1[3]), .c(HEX1[2]), .dp(HEX1[7]));
  Multiplexer #(.width(4)) multiplexer_2 (
    .in0(DownCounter_v1_1_count), .in1(Mod5_Counter_1_output_bus_1), .out(multiplexer_2_out),
    .sel(pedestrian_clock));
  _7_Segment_Display #(.active("false")) L_7_Segment_Display_2 (
    .g(HEX0[6]), .f(HEX0[5]), .a(HEX0[0]), .b(HEX0[1]), .e(HEX0[4]), .d(HEX0[3]), .c(HEX0[2]), .dp(HEX0[7]));
  pedestrian_button pedestrian_button_2 (.counter(Mod5_Counter_1_output_bus_1), .en(pedestrian_clock));
  Bin2Hex Bin2Hex_1 (
    .v3(multiplexer_2_out[3]), .v2(multiplexer_2_out[2]), .v1(multiplexer_2_out[1]),
    .v0(multiplexer_2_out[0]), .HEX1(HEX1), .HEX0(HEX0));

  // Notes on the sheet:
  //   Traffic Light A
  //   Traffic Light B
  //   Counter Display
endmodule

module Seg7_Decoder (
  input  i_m3,
  input  i_m2,
  input  i_m1,
  input  i_m0,
  output [7:0] o_seg
);

  wire and_1_out, and_2_out, and_3_out, and_4_out, and_5_out, and_6_out, and_7_out, and_8_out, and_9_out,
       and_10_out, and_11_out, and_12_out, and_13_out, and_14_out, and_15_out, and_16_out, and_17_out,
       and_18_out, and_19_out, and_20_out, and_21_out, and_22_out, and_23_out, not_1_out, not_2_out,
       not_3_out, not_4_out;

  not not_1 (not_1_out, i_m3);
  not not_2 (not_2_out, i_m2);
  not not_3 (not_3_out, i_m1);
  not not_4 (not_4_out, i_m0);
  and and_1 (and_1_out, not_1_out, not_2_out, not_3_out);
  and and_2 (and_2_out, not_1_out, i_m2, i_m1, i_m0);
  and and_3 (and_3_out, i_m3, not_2_out, i_m1);
  and and_4 (and_4_out, not_1_out, not_2_out, i_m0);
  and and_5 (and_5_out, not_1_out, not_2_out, i_m1);
  and and_6 (and_6_out, not_2_out, i_m1, i_m0);
  and and_7 (and_7_out, i_m3, i_m2, not_3_out);
  and and_8 (and_8_out, not_1_out, i_m2, not_3_out);
  and and_9 (and_9_out, i_m3, i_m2, i_m1);
  and and_10 (and_10_out, not_1_out, not_2_out, not_3_out, i_m0);
  and and_11 (and_11_out, not_1_out, i_m2, not_3_out, not_4_out);
  and and_12 (and_12_out, not_1_out, i_m2, i_m1, i_m0);
  and and_13 (and_13_out, i_m3, not_2_out, i_m1, i_m0);
  and and_14 (and_14_out, i_m3, i_m2, i_m1, not_4_out);
  and and_15 (and_15_out, not_1_out, not_2_out, i_m1, not_4_out);
  and and_16 (and_16_out, i_m3, i_m2, not_3_out, not_4_out);
  and and_17 (and_17_out, not_1_out, i_m2, not_3_out, i_m0);
  and and_18 (and_18_out, not_1_out, i_m2, i_m1, not_4_out);
  and and_19 (and_19_out, i_m3, i_m2, i_m1, i_m0);
  and and_20 (and_20_out, not_1_out, not_2_out, not_3_out, i_m0);
  and and_21 (and_21_out, not_1_out, i_m2, not_3_out, not_4_out);
  and and_22 (and_22_out, i_m3, not_2_out, i_m1, i_m0);
  and and_23 (and_23_out, i_m3, i_m2, i_m1, not_4_out);
  or or_1 (o_seg[6], and_1_out, and_2_out, and_3_out);
  or or_2 (o_seg[5], and_4_out, and_5_out, and_6_out, and_7_out);
  or or_3 (o_seg[4], i_m0, and_8_out, and_9_out);
  or or_4 (o_seg[3], and_10_out, and_11_out, and_12_out, and_13_out, and_14_out);
  or or_5 (o_seg[2], and_15_out, and_16_out);
  or or_6 (o_seg[1], and_17_out, and_18_out, and_19_out);
  or or_7 (o_seg[0], and_20_out, and_21_out, and_22_out, and_23_out);

  assign o_seg[7] = 1'b1;
endmodule

module CircuitA (
  input  i2,
  input  i1,
  input  i0,
  output o2,
  output o1,
  output o0
);

  not not_1 (o1, i1);
  and and_1 (o2, i2, i1);

  assign o0 = i0;
endmodule

module myComparator (
  input  v3,
  input  v2,
  input  v1,
  input  v0,
  output z
);

  wire and_1_out, and_2_out;

  and and_1 (and_1_out, v3, v1);
  and and_2 (and_2_out, v3, v2);
  or or_1 (z, and_1_out, and_2_out);
endmodule

module CircuitB (
  input  z,
  output s6,
  output s5,
  output s4,
  output s3,
  output s2,
  output s1,
  output s0
);


  assign s0 = z;
  assign s1 = 1'b0;
  assign s2 = 1'b0;
  assign s3 = z;
  assign s4 = z;
  assign s5 = z;
  assign s6 = 1'b1;
endmodule

module Bin2Hex (
  input  v3,
  input  v2,
  input  v1,
  input  v0,
  output [7:0] HEX1,
  output [7:0] HEX0
);

  wire z;

  myComparator myComparator_1 (.v3(v3), .v2(v2), .v1(v1), .v0(v0), .z(z));
  CircuitB CircuitB_1 (
    .z(z), .s6(HEX1[6]), .s5(HEX1[5]), .s4(HEX1[4]), .s3(HEX1[3]), .s2(HEX1[2]), .s1(HEX1[1]), .s0(HEX1[0]));
  Seg7_Decoder Seg7_Decoder_1 (.i_m3(v3), .i_m2(v2), .i_m1(v1), .i_m0(v0), .o_seg(HEX0));

  assign HEX1[7] = 1'b1;
endmodule

module pedestrian_button (
  input  [3:0] counter,
  output en
);

  or or_1 (en, counter[0], counter[1], counter[2], counter[3]);
endmodule

module DownCounter_v1 (
  input  en,
  input  clk,
  output [3:0] count
);

  wire and_1_out, and_2_out, and_3_out, and_4_out, t_ff_1_q, t_ff_2_q, t_ff_3_q;

  T_Flip_Flop t_ff_1 (.T(en), .clk(clk), .Q(t_ff_1_q), .Qn(count[0]));  // open: reset, preset
  and and_1 (and_1_out, count[0], count[1], count[2], count[3]);
  and and_2 (and_2_out, en, t_ff_1_q);
  T_Flip_Flop t_ff_2 (.T(and_2_out), .clk(clk), .Q(t_ff_2_q), .Qn(count[1]));  // open: reset, preset
  and and_3 (and_3_out, and_2_out, t_ff_2_q);
  T_Flip_Flop t_ff_3 (.T(and_3_out), .clk(clk), .Q(t_ff_3_q), .Qn(count[2]), .preset(and_1_out));  // open: reset
  and and_4 (and_4_out, and_3_out, t_ff_3_q);
  T_Flip_Flop t_ff_4 (.T(and_4_out), .clk(clk), .Qn(count[3]), .preset(and_1_out));  // open: Q, reset

  // Notes on the sheet:
  //   Synchronous Down Counter from 3 to 0 with reset
endmodule

module FSM (
  input  en,
  input  next_state,
  output G,
  output Y,
  output R,
  output rst
);

  wire [1:0] multiplexer_1_out, register_1_q;

  Multiplexer #(.select(3), .width(2)) multiplexer_1 (
    .in0(2'b00), .in1(2'b01), .in2(2'b10), .in4(2'b01), .in5(2'b10), .in6(2'b00), .out(multiplexer_1_out),
    .sel({en, register_1_q}));  // open: in3, in7
  Register #(.width(2)) register_1 (.D(multiplexer_1_out), .Q(register_1_q), .clk(next_state));  // open: en, clr
  // Probe on multiplexer_1_out
  // Probe on register_1_q
  buf and_1 (G, ~register_1_q[0]);  // AND_Gate AND_Gate
  buf and_2 (Y, register_1_q[0]);  // AND_Gate AND_Gate
  and and_3 (R, ~register_1_q[0], register_1_q[1]);  // AND_Gate

  assign rst = next_state;
endmodule

module FSM2 (
  input  en,
  input  next_state,
  output Ra,
  output Ya,
  output end_cycle_a,
  output Ga,
  output Rb,
  output Yb,
  output end_cycle_b,
  output Gb
);

  wire [3:0] FSM2_Pos_1_x;

  FSM2_Pos FSM2_Pos_1 (.en(en), .next_state(next_state), .x(FSM2_Pos_1_x));
  and and_1 (Ra, ~FSM2_Pos_1_x[2], FSM2_Pos_1_x[3]);  // AND_Gate
  and and_2 (Ya, FSM2_Pos_1_x[2], ~FSM2_Pos_1_x[3]);  // AND_Gate
  and and_3 (Ga, ~FSM2_Pos_1_x[2], ~FSM2_Pos_1_x[3]);  // AND_Gate
  and and_4 (Rb, ~FSM2_Pos_1_x[0], FSM2_Pos_1_x[1]);  // AND_Gate
  and and_5 (Yb, FSM2_Pos_1_x[0], ~FSM2_Pos_1_x[1]);  // AND_Gate
  and and_6 (Gb, ~FSM2_Pos_1_x[1], ~FSM2_Pos_1_x[0]);  // AND_Gate
  and and_7 (end_cycle_a, Ya, Rb);
  and and_8 (end_cycle_b, Ra, Yb);
endmodule

module FSM2_Pos (
  input  en,
  input  next_state,
  output [3:0] x
);

  wire and_1_out, and_3_out, not_1_out, not_2_out, not_3_out;
  wire [3:0] register_1_q;

  Register #(.width(4)) register_1 (.D(x), .en(en), .Q(register_1_q), .clk(next_state));  // open: clr
  not not_1 (not_1_out, register_1_q[3]);
  not not_2 (not_2_out, register_1_q[2]);
  not not_3 (not_3_out, register_1_q[0]);
  and and_1 (and_1_out, register_1_q[3], not_3_out);
  and and_2 (x[2], not_2_out, register_1_q[1]);
  and and_3 (and_3_out, not_1_out, not_2_out);
  and and_4 (x[0], register_1_q[3], not_3_out);
  or or_1 (x[3], register_1_q[2], and_1_out);
  or or_2 (x[1], register_1_q[0], and_3_out);
endmodule

module FA (
  input  x,
  input  y,
  input  c,
  output z,
  output cout
);

  wire and_1_out, and_2_out, and_3_out, and_4_out, and_5_out, and_6_out, and_7_out, not_1_out, not_2_out,
       not_3_out;

  not not_1 (not_1_out, x);
  not not_2 (not_2_out, y);
  not not_3 (not_3_out, c);
  and and_1 (and_1_out, not_1_out, not_2_out, c);
  and and_2 (and_2_out, not_1_out, y, not_3_out);
  and and_3 (and_3_out, x, not_2_out, not_3_out);
  and and_4 (and_4_out, x, y, c);
  and and_5 (and_5_out, y, c);
  and and_6 (and_6_out, x, c);
  or or_1 (cout, and_5_out, and_6_out, and_7_out);
  and and_7 (and_7_out, x, y);
  or or_2 (z, and_1_out, and_2_out, and_3_out, and_4_out);
endmodule

module RCAC (
  input  [3:0] Input_bus_1,
  input  [3:0] Input_bus_2,
  input  Input_1,
  output [3:0] z,
  output Cout
);

  wire FA_1_cout, FA_2_cout, FA_3_cout, xor_1_out, xor_2_out, xor_3_out, xor_4_out;

  xor xor_1 (xor_1_out, Input_bus_2[0], Input_1);
  xor xor_2 (xor_2_out, Input_bus_2[1], Input_1);
  xor xor_3 (xor_3_out, Input_bus_2[2], Input_1);
  xor xor_4 (xor_4_out, Input_bus_2[3], Input_1);
  FA FA_1 (.x(Input_bus_1[0]), .y(xor_1_out), .c(Input_1), .z(z[0]), .cout(FA_1_cout));
  FA FA_2 (.x(Input_bus_1[1]), .y(xor_2_out), .c(FA_1_cout), .z(z[1]), .cout(FA_2_cout));
  FA FA_3 (.x(Input_bus_1[2]), .y(xor_3_out), .c(FA_2_cout), .z(z[2]), .cout(FA_3_cout));
  FA FA_4 (.x(Input_bus_1[3]), .y(xor_4_out), .c(FA_3_cout), .z(z[3]), .cout(Cout));

  // Other names for the same wires on the sheet: x0 = Input_bus_1[0]; x1 = Input_bus_1[1]; x2 = Input_bus_1[2];
  //   x3 = Input_bus_1[3]; y0 = Input_bus_2[0]; y1 = Input_bus_2[1]; y2 = Input_bus_2[2]; y3 = Input_bus_2[3]
endmodule

module Mod5_Counter (
  input  E,
  input  Clk,
  input  [3:0] five_2ndcomp,
  output [3:0] Output_bus_1
);

  wire and_1_out, and_2_out, and_3_out, and_4_out, not_1_out;
  wire [3:0] not_2_out, t_ff_1_q;

  T_Flip_Flop t_ff_1 (.T(E), .clk(Clk), .Q(t_ff_1_q[0]), .reset(and_1_out));  // open: Qn, preset
  and and_1 (and_1_out, t_ff_1_q[0], not_1_out, t_ff_1_q[1], t_ff_1_q[3]);
  not not_1 (not_1_out, t_ff_1_q[2]);
  and and_2 (and_2_out, E, t_ff_1_q[0]);
  T_Flip_Flop t_ff_2 (.T(and_2_out), .clk(Clk), .Q(t_ff_1_q[1]), .reset(and_1_out));  // open: Qn, preset
  and and_3 (and_3_out, and_2_out, t_ff_1_q[1]);
  T_Flip_Flop t_ff_3 (.T(and_3_out), .clk(Clk), .Q(t_ff_1_q[2]), .reset(and_1_out));  // open: Qn, preset
  and and_4 (and_4_out, and_3_out, t_ff_1_q[2]);
  T_Flip_Flop t_ff_4 (.T(and_4_out), .clk(Clk), .Q(t_ff_1_q[3]), .reset(and_1_out));  // open: Qn, preset
  assign not_2_out = ~t_ff_1_q;  // NOT_Gate not_2, 4 bits wide
  RCAC RCAC_1 (.Input_bus_1(not_2_out), .Input_bus_2(five_2ndcomp), .Input_1(1'b0), .z(Output_bus_1));  // open: Cout
endmodule
