// Logisim project Lab_6.circ as structural Verilog
module main (
  input  Input_1,
  input  [3:0] Input_bus_1,
  input  Input_2
);

  wire b0, b1, b2, b3, b4, b5, b6, c0, c1, c2, c3, c4, c5, c6, clock_1_out, not_1_out;
  wire [3:0] Mod5_Template_1_output_bus_1;
  wire [7:7] Bin2Hex_1_hex0, Bin2Hex_1_hex1;

  Clock clock_1 (.out(clock_1_out));
  not not_1 (not_1_out, Input_2);
  Mod5_Template Mod5_Template_1 (
    .E(Input_1), .Clk(clock_1_out), .five_2ndcomp(Input_bus_1), .Reset(not_1_out),
    .Output_bus_1(Mod5_Template_1_output_bus_1));
  _7_Segment_Display #(.active("false")) L_7_Segment_Display_3 (
    .g(b6), .f(b5), .a(b0), .b(b1), .e(b4), .d(b3), .c(b2), .dp(1'b1));
  _7_Segment_Display #(.active("false")) L_7_Segment_Display_4 (
    .g(c6), .f(c5), .a(c0), .b(c1), .e(c4), .d(c3), .c(c2), .dp(1'b1));
  Bin2Hex Bin2Hex_1 (
    .v3(Mod5_Template_1_output_bus_1[3]), .v2(Mod5_Template_1_output_bus_1[2]),
    .v1(Mod5_Template_1_output_bus_1[1]), .v0(Mod5_Template_1_output_bus_1[0]),
    .HEX1({Bin2Hex_1_hex1[7], b6, b5, b4, b3, b2, b1, b0}),
    .HEX0({Bin2Hex_1_hex0[7], c6, c5, c4, c3, c2, c1, c0}));

  // Notes on the sheet:
  //   Counter Display
endmodule

module Seg7_Decoder (
  input  i_m3,
  input  i_m2,
  input  i_m1,
  input  i_m0,
  output [7:0] o_seg
);

  wire and_1_out, and_2_out, and_3_out, and_4_out, and_5_out, and_6_out, and_7_out, and_8_out, and_9_out,
       and_10_out, and_11_out, and_12_out, and_13_out, and_14_out, and_15_out, and_16_out, and_17_out,
       and_18_out, and_19_out, and_20_out, and_21_out, and_22_out, and_23_out, not_1_out, not_2_out,
       not_3_out, not_4_out;

  not not_1 (not_1_out, i_m3);
  not not_2 (not_2_out, i_m2);
  not not_3 (not_3_out, i_m1);
  not not_4 (not_4_out, i_m0);
  and and_1 (and_1_out, not_1_out, not_2_out, not_3_out);
  and and_2 (and_2_out, not_1_out, i_m2, i_m1, i_m0);
  and and_3 (and_3_out, i_m3, not_2_out, i_m1);
  and and_4 (and_4_out, not_1_out, not_2_out, i_m0);
  and and_5 (and_5_out, not_1_out, not_2_out, i_m1);
  and and_6 (and_6_out, not_2_out, i_m1, i_m0);
  and and_7 (and_7_out, i_m3, i_m2, not_3_out);
  and and_8 (and_8_out, not_1_out, i_m2, not_3_out);
  and and_9 (and_9_out, i_m3, i_m2, i_m1);
  and and_10 (and_10_out, not_1_out, not_2_out, not_3_out, i_m0);
  and and_11 (and_11_out, not_1_out, i_m2, not_3_out, not_4_out);
  and and_12 (and_12_out, not_1_out, i_m2, i_m1, i_m0);
  and and_13 (and_13_out, i_m3, not_2_out, i_m1, i_m0);
  and and_14 (and_14_out, i_m3, i_m2, i_m1, not_4_out);
  and and_15 (and_15_out, not_1_out, not_2_out, i_m1, not_4_out);
  and and_16 (and_16_out, i_m3, i_m2, not_3_out, not_4_out);
  and and_17 (and_17_out, not_1_out, i_m2, not_3_out, i_m0);
  and and_18 (and_18_out, not_1_out, i_m2, i_m1, not_4_out);
  and and_19 (and_19_out, i_m3, i_m2, i_m1, i_m0);
  and and_20 (and_20_out, not_1_out, not_2_out, not_3_out, i_m0);
  and and_21 (and_21_out, not_1_out, i_m2, not_3_out, not_4_out);
  and and_22 (and_22_out, i_m3, not_2_out, i_m1, i_m0);
  and and_23 (and_23_out, i_m3, i_m2, i_m1, not_4_out);
  or or_1 (o_seg[6], and_1_out, and_2_out, and_3_out);
  or or_2 (o_seg[5], and_4_out, and_5_out, and_6_out, and_7_out);
  or or_3 (o_seg[4], i_m0, and_8_out, and_9_out);
  or or_4 (o_seg[3], and_10_out, and_11_out, and_12_out, and_13_out, and_14_out);
  or or_5 (o_seg[2], and_15_out, and_16_out);
  or or_6 (o_seg[1], and_17_out, and_18_out, and_19_out);
  or or_7 (o_seg[0], and_20_out, and_21_out, and_22_out, and_23_out);

  assign o_seg[7] = 1'b1;
endmodule

module CircuitA (
  input  i2,
  input  i1,
  input  i0,
  output o2,
  output o1,
  output o0
);

  not not_1 (o1, i1);
  and and_1 (o2, i2, i1);

  assign o0 = i0;
endmodule

module myComparator (
  input  v3,
  input  v2,
  input  v1,
  input  v0,
  output z
);

  wire and_1_out, and_2_out;

  and and_1 (and_1_out, v3, v1);
  and and_2 (and_2_out, v3, v2);
  or or_1 (z, and_1_out, and_2_out);
endmodule

module CircuitB (
  input  z,
  output s6,
  output s5,
  output s4,
  output s3,
  output s2,
  output s1,
  output s0
);


  assign s0 = z;
  assign s1 = 1'b0;
  assign s2 = 1'b0;
  assign s3 = z;
  assign s4 = z;
  assign s5 = z;
  assign s6 = 1'b1;
endmodule

module Bin2Hex (
  input  v3,
  input  v2,
  input  v1,
  input  v0,
  output [7:0] HEX1,
  output [7:0] HEX0
);

  wire z;

  myComparator myComparator_1 (.v3(v3), .v2(v2), .v1(v1), .v0(v0), .z(z));
  CircuitB CircuitB_1 (
    .z(z), .s6(HEX1[6]), .s5(HEX1[5]), .s4(HEX1[4]), .s3(HEX1[3]), .s2(HEX1[2]), .s1(HEX1[1]), .s0(HEX1[0]));
  Seg7_Decoder Seg7_Decoder_1 (.i_m3(v3), .i_m2(v2), .i_m1(v1), .i_m0(v0), .o_seg(HEX0));

  assign HEX1[7] = 1'b1;
endmodule

module UpCounter_Template (
  input  E,
  input  Clk,
  output [3:0] Output_bus_1
);

  wire t_ff_1_qn, t_ff_2_qn, t_ff_3_qn;

  T_Flip_Flop t_ff_1 (.T(E), .clk(Clk), .Q(Output_bus_1[0]), .Qn(t_ff_1_qn));  // open: reset, preset
  T_Flip_Flop t_ff_2 (.T(E), .clk(t_ff_1_qn), .Q(Output_bus_1[1]), .Qn(t_ff_2_qn));  // open: reset, preset
  T_Flip_Flop t_ff_3 (.T(E), .clk(t_ff_2_qn), .Q(Output_bus_1[2]), .Qn(t_ff_3_qn));  // open: reset, preset
  T_Flip_Flop t_ff_4 (.T(E), .clk(t_ff_3_qn), .Q(Output_bus_1[3]));  // open: Qn, reset, preset
endmodule

module DownCounter_Template (
  input  E,
  input  Clk,
  output [3:0] Output_bus_1
);

  wire nand_1_out, not_1_out, t_ff_1_qn, t_ff_2_qn, t_ff_3_qn;

  T_Flip_Flop t_ff_1 (.T(E), .clk(Clk), .Q(Output_bus_1[0]), .Qn(t_ff_1_qn), .reset(not_1_out));  // open: preset
  T_Flip_Flop t_ff_2 (.T(E), .clk(t_ff_1_qn), .Q(Output_bus_1[1]), .Qn(t_ff_2_qn), .reset(not_1_out));  // open: preset
  T_Flip_Flop t_ff_3 (.T(E), .clk(t_ff_2_qn), .Q(Output_bus_1[2]), .Qn(t_ff_3_qn), .reset(not_1_out));  // open: preset
  T_Flip_Flop t_ff_4 (.T(E), .clk(t_ff_3_qn), .Q(Output_bus_1[3]), .reset(not_1_out));  // open: Qn, preset
  nand nand_1 (nand_1_out, Output_bus_1[0], Output_bus_1[3]);
  not not_1 (not_1_out, nand_1_out);
endmodule

module Mod5_Template (
  input  E,
  input  Clk,
  input  [3:0] five_2ndcomp,
  input  Reset,
  output [3:0] Output_bus_1
);

  wire and_1_out, and_2_out, and_3_out, and_4_out, not_1_out, or_1_out;
  wire [3:0] not_2_out, t_ff_1_q;

  or or_1 (or_1_out, and_1_out, Reset);
  T_Flip_Flop t_ff_1 (.T(E), .clk(Clk), .Q(t_ff_1_q[0]), .reset(or_1_out));  // open: Qn, preset
  and and_1 (and_1_out, t_ff_1_q[0], not_1_out, t_ff_1_q[1], t_ff_1_q[3]);
  not not_1 (not_1_out, t_ff_1_q[2]);
  and and_2 (and_2_out, E, t_ff_1_q[0]);
  T_Flip_Flop t_ff_2 (.T(and_2_out), .clk(Clk), .Q(t_ff_1_q[1]), .reset(or_1_out));  // open: Qn, preset
  and and_3 (and_3_out, and_2_out, t_ff_1_q[1]);
  T_Flip_Flop t_ff_3 (.T(and_3_out), .clk(Clk), .Q(t_ff_1_q[2]), .reset(or_1_out));  // open: Qn, preset
  and and_4 (and_4_out, and_3_out, t_ff_1_q[2]);
  T_Flip_Flop t_ff_4 (.T(and_4_out), .clk(Clk), .Q(t_ff_1_q[3]), .reset(or_1_out));  // open: Qn, preset
  assign not_2_out = ~t_ff_1_q;  // NOT_Gate not_2, 4 bits wide
  RCAC RCAC_1 (.Input_bus_1(not_2_out), .Input_bus_2(five_2ndcomp), .Input_1(1'b0), .z(Output_bus_1));  // open: Cout
endmodule

module HA (
  input  X,
  input  Y,
  output S,
  output C
);

  wire and_1_out, and_2_out, not_1_out, not_2_out;

  not not_1 (not_1_out, X);
  not not_2 (not_2_out, Y);
  and and_1 (and_1_out, not_1_out, Y);
  and and_2 (and_2_out, X, not_2_out);
  and and_3 (C, X, Y);
  or or_1 (S, and_1_out, and_2_out);
endmodule

module FA (
  input  x,
  input  y,
  input  c,
  output z,
  output cout
);

  wire and_1_out, and_2_out, and_3_out, and_4_out, and_5_out, and_6_out, and_7_out, not_1_out, not_2_out,
       not_3_out;

  not not_1 (not_1_out, x);
  not not_2 (not_2_out, y);
  not not_3 (not_3_out, c);
  and and_1 (and_1_out, not_1_out, not_2_out, c);
  and and_2 (and_2_out, not_1_out, y, not_3_out);
  and and_3 (and_3_out, x, not_2_out, not_3_out);
  and and_4 (and_4_out, x, y, c);
  and and_5 (and_5_out, y, c);
  and and_6 (and_6_out, x, c);
  or or_1 (cout, and_5_out, and_6_out, and_7_out);
  and and_7 (and_7_out, x, y);
  or or_2 (z, and_1_out, and_2_out, and_3_out, and_4_out);
endmodule

module RCA (
  input  [3:0] in_1,
  input  [3:0] in_2,
  input  in_3,
  output [3:0] z,
  output Cout
);

  wire fa_1_cout, fa_2_cout, fa_3_cout;

  FA fa_1 (.x(in_1[0]), .y(in_2[0]), .c(in_3), .z(z[0]), .cout(fa_1_cout));
  FA fa_2 (.x(in_1[1]), .y(in_2[1]), .c(fa_1_cout), .z(z[1]), .cout(fa_2_cout));
  FA fa_3 (.x(in_1[2]), .y(in_2[2]), .c(fa_2_cout), .z(z[2]), .cout(fa_3_cout));
  FA fa_4 (.x(in_1[3]), .y(in_2[3]), .c(fa_3_cout), .z(z[3]), .cout(Cout));

  // Other names for the same wires on the sheet: x0 = in_1[0]; x1 = in_1[1]; x2 = in_1[2]; x3 = in_1[3]; y0 = in_2[0];
  //   y1 = in_2[1]; y2 = in_2[2]; y3 = in_2[3]
endmodule

module RCAC (
  input  [3:0] Input_bus_1,
  input  [3:0] Input_bus_2,
  input  Input_1,
  output [3:0] z,
  output Cout
);

  wire FA_1_cout, FA_2_cout, FA_3_cout, xor_1_out, xor_2_out, xor_3_out, xor_4_out;

  xor xor_1 (xor_1_out, Input_bus_2[0], Input_1);
  xor xor_2 (xor_2_out, Input_bus_2[1], Input_1);
  xor xor_3 (xor_3_out, Input_bus_2[2], Input_1);
  xor xor_4 (xor_4_out, Input_bus_2[3], Input_1);
  FA FA_1 (.x(Input_bus_1[0]), .y(xor_1_out), .c(Input_1), .z(z[0]), .cout(FA_1_cout));
  FA FA_2 (.x(Input_bus_1[1]), .y(xor_2_out), .c(FA_1_cout), .z(z[1]), .cout(FA_2_cout));
  FA FA_3 (.x(Input_bus_1[2]), .y(xor_3_out), .c(FA_2_cout), .z(z[2]), .cout(FA_3_cout));
  FA FA_4 (.x(Input_bus_1[3]), .y(xor_4_out), .c(FA_3_cout), .z(z[3]), .cout(Cout));

  // Other names for the same wires on the sheet: x0 = Input_bus_1[0]; x1 = Input_bus_1[1]; x2 = Input_bus_1[2];
  //   x3 = Input_bus_1[3]; y0 = Input_bus_2[0]; y1 = Input_bus_2[1]; y2 = Input_bus_2[2]; y3 = Input_bus_2[3]
endmodule
