// Logisim project Lab_8.circ as structural Verilog: 2 circuits, main circuit main
module main (
  input  Input_1,
  input  Input_2,
  input  Input_3,
  output Output_1,
  output Output_2,
  output Output_3
);

  wire and_1_out, and_2_out, and_3_out, clk, clock_test_1_out_2, not_1_out;
  wire [2:1] counter_1_q;

  Clock clock_1 (.out(clk));
  and and_1 (and_1_out, Input_1, ~Input_2, ~Input_3, clk);  // AND_Gate
  and and_2 (and_2_out, Input_2, ~Input_1, ~Input_3, clk);  // AND_Gate
  and and_3 (and_3_out, Input_3, ~Input_1, ~Input_2, clock_test_1_out_2);  // AND_Gate
  clock_test clock_test_1 (.in_1(clk), .out_2(clock_test_1_out_2));
  Counter #(.max('h7), .width(3)) counter_1 (
    .Q({counter_1_q, Output_1}), .clk(and_1_out), .clr(not_1_out));  // open: load, D, count, carry, up
  not not_1 (not_1_out, Input_1);
  or or_1 (Output_2, counter_1_q[1], and_2_out);
  or or_2 (Output_3, counter_1_q[2], and_3_out);

  // Other names for the same wires on the sheet: in_0 = Input_1; in_1 = Input_2; in_2 = Input_3
endmodule

module clock_test (
  input  in_1,
  output out_2
);

  wire t_ff_1_q;

  T_Flip_Flop t_ff_1 (.T(in_1), .clk(in_1), .Q(t_ff_1_q));  // open: Qn, reset, preset
  T_Flip_Flop t_ff_2 (.T(t_ff_1_q), .clk(t_ff_1_q), .Q(out_2));  // open: Qn, reset, preset
endmodule
